# Fritzing sketch sender_monitor_schema (saved by Fritzing 0.9.3b)
perfboards: 1

parts:
  Part1 = Arduino Pro Mini v13
  Part2 = Soil Moisture Sensor
  U1 = RF-LINK_TX [package=rf-link_tx]
  Q2 = PNP-Transistor [package="TO92 [THT]"]  # not connected
  R2 = Resistor [tolerance=±5% resistance=220 package=THT]  # not connected
  VCC1 = Battery  # not connected

nets:
  N1: Part1.A0, Part2.SIG
  N2: Part1.D11_PWM/MOSI, U1.DATA
